// Logisim project Project.circ as structural Verilog: 4 circuits, main circuit Datapath
module Register_file (
  input  [3:0] Read_Reg_1,
  input  [31:0] Write_Data,
  input  WriteEn,
  input  [3:0] Read_Reg_2,
  input  CLK,
  input  [3:0] Write_Register,
  output [31:0] Read_Data_1,
  output [31:0] Read_Data_2
);

  wire and_1_out, and_2_out, and_3_out, and_4_out, and_5_out, and_6_out, and_7_out, and_8_out, and_9_out,
       and_10_out, and_11_out, and_12_out, and_13_out, and_14_out, and_15_out, and_16_out, decoder_1_out0,
       decoder_1_out1, decoder_1_out2, decoder_1_out3, decoder_1_out4, decoder_1_out5, decoder_1_out6,
       decoder_1_out7, decoder_1_out8, decoder_1_out9, decoder_1_out10, decoder_1_out11, decoder_1_out12,
       decoder_1_out13, decoder_1_out14, decoder_1_out15;
  wire [31:0] R0_q, R1_q, R2_q, R3_q, R4_q, R5_q, R6_q, R7_q, R8_q, R9_q, R10_q, R11_q, R12_q, R13_q, R14_q,
       R15_q;

  Decoder #(.select(4), .enable("false")) decoder_1 (
    .out0(decoder_1_out0), .out1(decoder_1_out1), .out2(decoder_1_out2), .out3(decoder_1_out3),
    .out4(decoder_1_out4), .out5(decoder_1_out5), .out6(decoder_1_out6), .out7(decoder_1_out7),
    .out8(decoder_1_out8), .out9(decoder_1_out9), .out10(decoder_1_out10), .out11(decoder_1_out11),
    .out12(decoder_1_out12), .out13(decoder_1_out13), .out14(decoder_1_out14), .out15(decoder_1_out15),
    .sel(Write_Register));
  and and_1 (and_1_out, WriteEn, decoder_1_out0);
  and and_2 (and_2_out, WriteEn, decoder_1_out1);
  and and_3 (and_3_out, WriteEn, decoder_1_out2);
  and and_4 (and_4_out, WriteEn, decoder_1_out3);
  and and_5 (and_5_out, WriteEn, decoder_1_out4);
  and and_6 (and_6_out, WriteEn, decoder_1_out5);
  and and_7 (and_7_out, WriteEn, decoder_1_out6);
  and and_8 (and_8_out, WriteEn, decoder_1_out7);
  and and_9 (and_9_out, WriteEn, decoder_1_out8);
  and and_10 (and_10_out, WriteEn, decoder_1_out9);
  and and_11 (and_11_out, WriteEn, decoder_1_out10);
  and and_12 (and_12_out, WriteEn, decoder_1_out11);
  and and_13 (and_13_out, WriteEn, decoder_1_out12);
  and and_14 (and_14_out, WriteEn, decoder_1_out13);
  and and_15 (and_15_out, WriteEn, decoder_1_out14);
  and and_16 (and_16_out, WriteEn, decoder_1_out15);
  Register #(.width(32)) R0 (.D(Write_Data), .en(and_1_out), .Q(R0_q), .clk(CLK));  // open: clr
  Register #(.width(32)) R1 (.D(Write_Data), .en(and_2_out), .Q(R1_q), .clk(CLK));  // open: clr
  Register #(.width(32)) R2 (.D(Write_Data), .en(and_3_out), .Q(R2_q), .clk(CLK));  // open: clr
  Register #(.width(32)) R3 (.D(Write_Data), .en(and_4_out), .Q(R3_q), .clk(CLK));  // open: clr
  Register #(.width(32)) R4 (.D(Write_Data), .en(and_5_out), .Q(R4_q), .clk(CLK));  // open: clr
  Register #(.width(32)) R5 (.D(Write_Data), .en(and_6_out), .Q(R5_q), .clk(CLK));  // open: clr
  Register #(.width(32)) R6 (.D(Write_Data), .en(and_7_out), .Q(R6_q), .clk(CLK));  // open: clr
  Register #(.width(32)) R7 (.D(Write_Data), .en(and_8_out), .Q(R7_q), .clk(CLK));  // open: clr
  Register #(.width(32)) R8 (.D(Write_Data), .en(and_9_out), .Q(R8_q), .clk(CLK));  // open: clr
  Register #(.width(32)) R9 (.D(Write_Data), .en(and_10_out), .Q(R9_q), .clk(CLK));  // open: clr
  Register #(.width(32)) R10 (.D(Write_Data), .en(and_11_out), .Q(R10_q), .clk(CLK));  // open: clr
  Register #(.width(32)) R11 (.D(Write_Data), .en(and_12_out), .Q(R11_q), .clk(CLK));  // open: clr
  Register #(.width(32)) R12 (.D(Write_Data), .en(and_13_out), .Q(R12_q), .clk(CLK));  // open: clr
  Register #(.width(32)) R13 (.D(Write_Data), .en(and_14_out), .Q(R13_q), .clk(CLK));  // open: clr
  Register #(.width(32)) R14 (.D(Write_Data), .en(and_15_out), .Q(R14_q), .clk(CLK));  // open: clr
  Register #(.width(32)) R15 (.D(Write_Data), .en(and_16_out), .Q(R15_q), .clk(CLK));  // open: clr
  Multiplexer #(.select(4), .width(32), .enable("false")) multiplexer_1 (
    .in0(R0_q), .in1(R1_q), .in2(R2_q), .in3(R3_q), .in4(R4_q), .in5(R5_q), .in6(R6_q), .in7(R7_q),
    .in8(R8_q), .in9(R9_q), .in10(R10_q), .in11(R11_q), .in12(R12_q), .in13(R13_q), .in14(R14_q),
    .in15(R15_q), .out(Read_Data_1), .sel(Read_Reg_1));
  Multiplexer #(.select(4), .width(32), .enable("false")) multiplexer_2 (
    .in0(R0_q), .in1(R1_q), .in2(R2_q), .in3(R3_q), .in4(R4_q), .in5(R5_q), .in6(R6_q), .in7(R7_q),
    .in8(R8_q), .in9(R9_q), .in10(R10_q), .in11(R11_q), .in12(R12_q), .in13(R13_q), .in14(R14_q),
    .in15(R15_q), .out(Read_Data_2), .sel(Read_Reg_2));
endmodule

module Control_unit (
  input  [5:0] in_1,
  output [2:0] ALUOp,
  output Binv,
  output Cout,
  output WriteReg,
  output Mem2reg,
  output ALU_Src,
  output RegDest,
  output Str,
  output Ld,
  output MemSelect,
  output Jump,
  output BEQ
);

  wire decoder_1_out0, decoder_1_out2, decoder_1_out5, decoder_1_out6, decoder_1_out7, decoder_1_out10;
  wire [3:0] bit_extender_1_out;

  Bit_Extender #(.in_width(6), .out_width(4)) bit_extender_1 (.in(in_1), .out(bit_extender_1_out));
  Decoder #(.select(4), .enable("false")) decoder_1 (
    .out0(decoder_1_out0), .out1(Str), .out2(decoder_1_out2), .out3(Ld), .out4(BEQ), .out5(decoder_1_out5),
    .out6(decoder_1_out6), .out7(decoder_1_out7), .out8(Binv), .out9(Jump), .out10(decoder_1_out10),
    .sel(bit_extender_1_out));  // open: out11, out12, out13, out14, out15
  or or_1 (ALU_Src, decoder_1_out0, Str, decoder_1_out2, Ld, decoder_1_out7);
  or or_2 (ALUOp[0], Str, decoder_1_out2, Ld, BEQ, decoder_1_out5, decoder_1_out7, Binv, Jump);
  or or_3 (ALUOp[1], BEQ, decoder_1_out6, decoder_1_out7, Jump);
  or or_4 (ALUOp[2], BEQ, Jump, decoder_1_out10);
  or or_5 (RegDest, decoder_1_out0, decoder_1_out2, Ld, decoder_1_out7);
  or or_6 (MemSelect, Str, Ld);
  or or_7 (WriteReg, decoder_1_out0, decoder_1_out2, Ld, decoder_1_out5, decoder_1_out6, decoder_1_out7, Binv, decoder_1_out10);

  assign Cout = Binv;
  assign Mem2reg = Ld;
endmodule

module Datapath (
  output [5:0] Opcode,
  output [3:0] Rs,
  output [3:0] Rt_Rd,
  output [3:0] Rd_I,
  output [31:0] out_5
);

  wire and_1_out, button_1_out, control_unit_1_alu_src, control_unit_1_beq, control_unit_1_binv,
       control_unit_1_cout, control_unit_1_jump, control_unit_1_ld, control_unit_1_mem2reg,
       control_unit_1_memselect, control_unit_1_regdest, control_unit_1_str, control_unit_1_writereg,
       new_alu_1_zero;
  wire [2:0] control_unit_1_aluop;
  wire [3:0] bit_extender_1_out, multiplexer_1_out;
  wire [14:0] Row1, Row2, Row3, Row4, Row5, Row6, Row7, Row8, Row9, Row_10;
  wire [15:0] adder_1_out, bit_extender_2_out, bit_extender_5_out, multiplexer_3_out, multiplexer_5_out,
       register_1_q;
  wire [23:0] bit_extender_4_out;
  wire [31:0] bit_extender_3_out, multiplexer_2_out, multiplexer_4_out, ram_1_data,
       register_file_1_read_data_1, register_file_1_read_data_2;

  Button button_1 (.out(button_1_out));
  Register #(.width(16)) register_1 (
    .D(multiplexer_5_out), .en(button_1_out), .Q(register_1_q), .clk(button_1_out));  // open: clr
  ROM #(.addrWidth(16), .dataWidth(18)) rom_1 (.addr(register_1_q), .data({Opcode, Rs, Rt_Rd, Rd_I}));  // open: sel
  Bit_Extender #(.in_width(6), .out_width(4)) bit_extender_1 (.in(Opcode), .out(bit_extender_1_out));
  Multiplexer #(.width(4), .enable("false")) multiplexer_1 (
    .in0(Rd_I), .in1(Rt_Rd), .out(multiplexer_1_out), .sel(control_unit_1_regdest));
  Control_unit control_unit_1 (
    .in_1(Opcode), .ALUOp(control_unit_1_aluop), .Binv(control_unit_1_binv), .Cout(control_unit_1_cout),
    .WriteReg(control_unit_1_writereg), .Mem2reg(control_unit_1_mem2reg), .ALU_Src(control_unit_1_alu_src),
    .RegDest(control_unit_1_regdest), .Str(control_unit_1_str), .Ld(control_unit_1_ld),
    .Jump(control_unit_1_jump), .BEQ(control_unit_1_beq), .MemSelect(control_unit_1_memselect));
  ROM #(.addrWidth(4), .dataWidth(15)) rom_2 (.addr(bit_extender_1_out), .data(Row1));  // open: sel
  ROM #(.addrWidth(4), .dataWidth(15)) rom_3 (.addr(bit_extender_1_out), .data(Row2));  // open: sel
  ROM #(.addrWidth(4), .dataWidth(15)) rom_4 (.addr(bit_extender_1_out), .data(Row3));  // open: sel
  ROM #(.addrWidth(4), .dataWidth(15)) rom_5 (.addr(bit_extender_1_out), .data(Row4));  // open: sel
  assign bit_extender_2_out = {{4{1'b0}}, {Rs, Rt_Rd, Rd_I}};  // Bit_Extender bit_extender_2
  assign bit_extender_3_out = {{28{1'b0}}, Rd_I};  // Bit_Extender bit_extender_3
  ROM #(.addrWidth(4), .dataWidth(15)) rom_6 (.addr(bit_extender_1_out), .data(Row5));  // open: sel
  ROM #(.addrWidth(4), .dataWidth(15)) rom_7 (.addr(bit_extender_1_out), .data(Row6));  // open: sel
  ROM #(.addrWidth(4), .dataWidth(15)) rom_8 (.addr(bit_extender_1_out), .data(Row7));  // open: sel
  ROM #(.addrWidth(4), .dataWidth(15)) rom_9 (.addr(bit_extender_1_out), .data(Row8));  // open: sel
  DotMatrix #(.inputtype("row"), .matrixcols(15), .matrixrows(10)) dotmatrix_1 (
    .row0(Row1), .row1(Row2), .row2(Row3), .row3(Row4), .row4(Row5), .row5(Row6), .row6(Row7), .row7(Row8),
    .row8(Row9), .row9(Row_10));
  Register_file register_file_1 (
    .Read_Reg_1(Rs), .Write_Data(multiplexer_4_out), .WriteEn(control_unit_1_writereg), .Read_Reg_2(Rt_Rd),
    .CLK(button_1_out), .Write_Register(multiplexer_1_out), .Read_Data_1(register_file_1_read_data_1),
    .Read_Data_2(register_file_1_read_data_2));
  ROM #(.addrWidth(4), .dataWidth(15)) rom_10 (.addr(bit_extender_1_out), .data(Row9));  // open: sel
  ROM #(.addrWidth(4), .dataWidth(15)) rom_11 (.addr(bit_extender_1_out), .data(Row_10));  // open: sel
  New_ALU new_alu_1 (
    .A(register_file_1_read_data_1), .Binv(control_unit_1_binv), .B(multiplexer_2_out),
    .Cin(control_unit_1_cout), .S(out_5), .ALUop(control_unit_1_aluop), .Zero(new_alu_1_zero));  // open: Cout
  Multiplexer #(.width(32), .enable("false")) multiplexer_2 (
    .in0(register_file_1_read_data_2), .in1(bit_extender_3_out), .out(multiplexer_2_out),
    .sel(control_unit_1_alu_src));
  Adder #(.width(16)) adder_1 (.a(16'h1), .b(register_1_q), .out(adder_1_out));  // open: cin, cout
  and and_1 (and_1_out, new_alu_1_zero, control_unit_1_beq);
  Bit_Extender #(.in_width(32), .out_width(24)) bit_extender_4 (.in(out_5), .out(bit_extender_4_out));
  Bit_Extender #(.in_width(32)) bit_extender_5 (.in(bit_extender_3_out), .out(bit_extender_5_out));
  RAM #(.addrWidth(24), .dataWidth(32), .bus("separate")) ram_1 (
    .addr(bit_extender_4_out), .din(register_file_1_read_data_2), .data(ram_1_data),
    .str(control_unit_1_str), .sel(control_unit_1_memselect), .clk(button_1_out), .ld(control_unit_1_ld));  // open: clr
  Multiplexer #(.width(16), .enable("false")) multiplexer_3 (
    .in0(adder_1_out), .in1(bit_extender_5_out), .out(multiplexer_3_out), .sel(and_1_out));
  Multiplexer #(.width(32), .enable("false")) multiplexer_4 (
    .in0(out_5), .in1(ram_1_data), .out(multiplexer_4_out), .sel(control_unit_1_mem2reg));
  Multiplexer #(.width(16), .enable("false")) multiplexer_5 (
    .in0(multiplexer_3_out), .in1(bit_extender_2_out), .out(multiplexer_5_out), .sel(control_unit_1_jump));

  // Notes on the sheet:
  //   contents of rom_1 (hex, n*v repeats v):
  //   0 5231
  //   contents of rom_3 (hex, n*v repeats v):
  //   0 7c82 0 1000 5*0 800 2
  //   contents of rom_4 (hex, n*v repeats v):
  //   0 4082 2 1000 2000 42 4*0 2
  //   contents of rom_5 (hex, n*v repeats v):
  //   0 4082 88 1000 2000 42 7910 7910 7810 800 2
  //   contents of rom_6 (hex, n*v repeats v):
  //   0 7c92 73ba 1208 21ee 42 4138 4110 4010 a17 3c82
  //   contents of rom_7 (hex, n*v repeats v):
  //   73dc 4aa 52aa 1248 3d2a 79ce 7910 7910 7a5c b35 24ee
  //   contents of rom_8 (hex, n*v repeats v):
  //   5254 4c6 7bba 12a8 25ee 4a52 910 910 a54 ad7 24aa
  //   contents of rom_9 (hex, n*v repeats v):
  //   525c 7c82 0 1318 2502 4a52 7918 7910 7bdc 3a14 3eae
  //   Opcode mnemonic
  //   contents of rom_10 (hex, n*v repeats v):
  //   53d0 0 0 1208 3de2 7dce
  //   contents of rom_11 (hex, n*v repeats v):
  //   10
endmodule

module New_ALU (
  input  Cin,
  input  [31:0] A,
  input  Binv,
  input  [31:0] B,
  input  [2:0] ALUop,
  output [31:0] S,
  output Cout,
  output Zero
);

  wire comparator_1_lt;
  wire [4:0] bit_extender_1_out;
  wire [31:0] adder_1_out, and_1_out, bit_extender_2_out, multiplexer_1_out, not_1_out, shifter_1_out;

  assign not_1_out = ~B;  // NOT_Gate not_1, 32 bits wide
  Bit_Extender #(.in_width(32), .out_width(5)) bit_extender_1 (.in(B), .out(bit_extender_1_out));
  Multiplexer #(.width(32), .enable("false")) multiplexer_1 (
    .in0(B), .in1(not_1_out), .out(multiplexer_1_out), .sel(Binv));
  Comparator #(.width(32)) comparator_1 (.a(A), .b(B), .eq(Zero), .lt(comparator_1_lt));  // open: gt
  Shifter #(.width(32)) shifter_1 (.in(A), .\dist (bit_extender_1_out), .out(shifter_1_out));
  Adder #(.width(32)) adder_1 (.a(A), .b(multiplexer_1_out), .out(adder_1_out), .cin(Cin), .cout(Cout));
  assign bit_extender_2_out = {{31{1'b0}}, comparator_1_lt};  // Bit_Extender bit_extender_2
  assign and_1_out = A & B;  // AND_Gate and_1, 32 bits wide
  Multiplexer #(.select(3), .width(32), .enable("false")) multiplexer_2 (
    .in0(shifter_1_out), .in1(adder_1_out), .in2(bit_extender_2_out), .in3(shifter_1_out), .in4(and_1_out),
    .out(S), .sel(ALUop));  // open: in5, in6, in7
endmodule
